// Logisim project control_logic.circ as structural Verilog: 8 circuits, main circuit control_logic
module control_logic (
  input  [31:0] inst,
  input  BrEq,
  input  BrLt,
  output PCSel,
  output RegWEn,
  output [2:0] ImmSel,
  output BrUn,
  output ASel,
  output BSel,
  output [3:0] ALUSel,
  output MemRW,
  output [1:0] WBSel,
  output BrSel
);

  RegWEn_processor regwen_processor_1 (.Opcode(inst[6:0]), .RegWEn(RegWEn));
  ASel_processor asel_processor_1 (.Opcode(inst[6:0]), .ASel(ASel));
  MemRW_processor memrw_processor_1 (.Opcode(inst[6:0]), .func3(inst[14:12]), .BrEq(BrEq), .BrLt(BrLt), .MemRW(MemRW));
  WBSel_processor wbsel_processor_1 (.Opcode(inst[6:0]), .func3(inst[14:12]), .WBSel(WBSel));
  BrUn_processor brun_processor_1 (.Opcode(inst[6:0]), .func3(inst[14:12]), .BrUn(BrUn));
  BSel_processor bsel_processor_1 (.Opcode(inst[6:0]), .BSel(BSel));
  PCSel_processor pcsel_processor_1 (.Opcode(inst[6:0]), .func3(inst[14:12]), .BrEq(BrEq), .BrLt(BrLt), .PCSel(PCSel));

  // Other names for the same wires on the sheet: Opcode[6:0] = inst[6:0]; func3[2:0] = inst[14:12];
  //   func7[6:0] = inst[31:25]

  // Notes on the sheet:
  //   INPUTS to your circuit
  //   DON'T CHANGE THE LOCATIONS OF THE INPUTS AND OUTPUTS!
  //   OUTPUT from your circuit
endmodule

module RegWEn_processor (
  input  [6:0] Opcode,
  output RegWEn
);

  wire and_1_out, not_1_out, not_2_out, not_3_out;

  not not_1 (not_1_out, Opcode[2]);
  not not_2 (not_2_out, Opcode[3]);
  not not_3 (not_3_out, Opcode[4]);
  and and_1 (and_1_out, not_1_out, not_2_out, not_3_out, Opcode[5]);
  not not_4 (RegWEn, and_1_out);

  // Notes on the sheet:
  //   INPUT
  //   OUTPUT
endmodule

module BrUn_processor (
  input  [6:0] Opcode,
  input  [2:0] func3,
  output BrUn
);

  wire not_1_out, not_2_out, not_3_out;

  not not_1 (not_1_out, Opcode[2]);
  not not_2 (not_2_out, Opcode[3]);
  not not_3 (not_3_out, Opcode[4]);
  and and_1 (BrUn, not_1_out, not_2_out, not_3_out, Opcode[5], Opcode[6], func3[1], func3[2]);

  // Notes on the sheet:
  //   INPUT
  //   OUTPUT
endmodule

module ASel_processor (
  input  [6:0] Opcode,
  output ASel
);

  wire ASel_B, ASel_J, ASel_U, not_1_out, not_2_out, not_3_out, not_4_out, not_5_out, not_6_out;

  not not_1 (not_1_out, Opcode[2]);
  not not_2 (not_2_out, Opcode[3]);
  not not_3 (not_3_out, Opcode[4]);
  not not_4 (not_4_out, Opcode[4]);
  not not_5 (not_5_out, Opcode[3]);
  not not_6 (not_6_out, Opcode[6]);
  and and_1 (ASel_B, not_1_out, not_2_out, not_3_out, Opcode[5], Opcode[6]);
  and and_2 (ASel_J, Opcode[2], Opcode[3], not_4_out, Opcode[5], Opcode[6]);
  and and_3 (ASel_U, Opcode[2], not_5_out, Opcode[4], not_6_out);
  or or_1 (ASel, ASel_B, ASel_J, ASel_U);

  // Notes on the sheet:
  //   INPUT
  //   OUTPUT
endmodule

module BSel_processor (
  input  [6:0] Opcode,
  output BSel
);

  wire and_1_out, not_1_out, not_2_out, not_3_out;

  not not_1 (not_1_out, Opcode[2]);
  not not_2 (not_2_out, Opcode[3]);
  not not_3 (not_3_out, Opcode[6]);
  and and_1 (and_1_out, not_1_out, not_2_out, Opcode[4], Opcode[5], not_3_out);
  not not_4 (BSel, and_1_out);

  // Notes on the sheet:
  //   INPUT
  //   OUTPUT
endmodule

module MemRW_processor (
  input  [6:0] Opcode,
  input  [2:0] func3,
  input  BrEq,
  input  BrLt,
  output MemRW
);

  wire and_1_out, is_S, is_sw, not_1_out, not_2_out, not_3_out, not_4_out, not_5_out, not_6_out;

  not not_1 (not_1_out, Opcode[2]);
  not not_2 (not_2_out, Opcode[3]);
  not not_3 (not_3_out, Opcode[4]);
  not not_4 (not_4_out, Opcode[6]);
  not not_5 (not_5_out, func3[0]);
  not not_6 (not_6_out, func3[2]);
  and and_1 (and_1_out, not_1_out, not_2_out, not_3_out, Opcode[5], not_4_out);
  and and_2 (is_sw, not_5_out, func3[1], not_6_out);
  not not_7 (is_S, and_1_out);
  and and_3 (MemRW, is_S, is_sw);

  // Notes on the sheet:
  //   INPUT
  //   OUTPUT
endmodule

module PCSel_processor (
  input  [6:0] Opcode,
  input  [2:0] func3,
  input  BrEq,
  input  BrLt,
  output PCSel
);

  wire func3_000, func3_001, func3_100, func3_101, func3_110, func3_111, or_1_out, PCSel_B;

  Multiplexer #(.select(2), .enable("false")) multiplexer_1 (
    .in0(1'b0), .in1(1'b0), .in2(1'b1), .out(func3_000), .sel({BrEq, BrLt}));  // open: in3
  Multiplexer #(.select(2), .enable("false")) multiplexer_2 (
    .in0(1'b1), .in1(1'b0), .in2(1'b1), .out(func3_101), .sel({BrEq, BrLt}));  // open: in3
  or or_1 (or_1_out, Opcode[2], PCSel_B);
  and and_1 (PCSel, Opcode[6], or_1_out);
  Multiplexer #(.select(2), .enable("false")) multiplexer_3 (
    .in0(1'b1), .in1(1'b1), .in2(1'b0), .out(func3_001), .sel({BrEq, BrLt}));  // open: in3
  Multiplexer #(.select(2), .enable("false")) multiplexer_4 (
    .in0(1'b0), .in1(1'b1), .in2(1'b0), .out(func3_110), .sel({BrEq, BrLt}));  // open: in3
  Multiplexer #(.select(3), .enable("false")) multiplexer_5 (
    .in0(func3_000), .in1(func3_001), .in4(func3_100), .in5(func3_101), .in6(func3_110), .in7(func3_111),
    .out(PCSel_B), .sel(func3));  // open: in2, in3
  Multiplexer #(.select(2), .enable("false")) multiplexer_6 (
    .in0(1'b0), .in1(1'b1), .in2(1'b0), .out(func3_100), .sel({BrEq, BrLt}));  // open: in3
  Multiplexer #(.select(2), .enable("false")) multiplexer_7 (
    .in0(1'b1), .in1(1'b0), .in2(1'b1), .out(func3_111), .sel({BrEq, BrLt}));  // open: in3

  // Other names for the same wires on the sheet: Br[1:0] = {BrEq, BrLt}; funct3[2:0] = func3

  // Notes on the sheet:
  //   INPUT
  //   OUTPUT
endmodule

module WBSel_processor (
  input  [6:0] Opcode,
  input  [2:0] func3,
  output [1:0] WBSel
);

  wire is_auipc, is_I_ALU, is_I_load, is_J, is_jalr, is_lui, is_R, not_1_out, not_2_out, not_3_out,
       not_4_out, not_5_out, not_6_out, not_7_out, not_8_out, not_9_out, not_10_out, not_11_out, not_12_out,
       not_13_out, not_14_out, not_15_out, not_16_out, not_17_out, not_18_out, not_19_out, not_20_out,
       OUT01_ALU, OUT10_PC_4;
  wire [1:0] bitfinder_1_index;

  not not_1 (not_1_out, Opcode[2]);
  not not_2 (not_2_out, Opcode[3]);
  not not_3 (not_3_out, Opcode[6]);
  not not_4 (not_4_out, Opcode[2]);
  not not_5 (not_5_out, Opcode[3]);
  not not_6 (not_6_out, Opcode[5]);
  not not_7 (not_7_out, Opcode[6]);
  not not_8 (not_8_out, Opcode[3]);
  not not_9 (not_9_out, Opcode[5]);
  not not_10 (not_10_out, Opcode[6]);
  not not_11 (not_11_out, Opcode[4]);
  not not_12 (not_12_out, Opcode[2]);
  not not_13 (not_13_out, Opcode[3]);
  not not_14 (not_14_out, Opcode[4]);
  not not_15 (not_15_out, Opcode[5]);
  not not_16 (not_16_out, Opcode[6]);
  not not_17 (not_17_out, Opcode[3]);
  not not_18 (not_18_out, Opcode[6]);
  not not_19 (not_19_out, Opcode[3]);
  not not_20 (not_20_out, Opcode[4]);
  and and_1 (is_R, not_1_out, not_2_out, Opcode[4], Opcode[5], not_3_out);
  and and_2 (is_I_ALU, not_4_out, not_5_out, Opcode[4], not_6_out, not_7_out);
  and and_3 (is_auipc, Opcode[2], not_8_out, Opcode[4], not_9_out, not_10_out);
  and and_4 (is_J, Opcode[2], Opcode[3], not_11_out, Opcode[5], Opcode[6]);
  and and_5 (is_I_load, not_12_out, not_13_out, not_14_out, not_15_out, not_16_out);
  and and_6 (is_lui, Opcode[2], not_17_out, Opcode[4], Opcode[5], not_18_out);
  and and_7 (is_jalr, Opcode[2], not_19_out, not_20_out, Opcode[5], Opcode[6]);
  or or_1 (OUT01_ALU, is_R, is_auipc, is_I_ALU);
  or or_2 (OUT10_PC_4, is_J, is_jalr);
  Multiplexer #(.select(2), .width(2), .enable("false")) multiplexer_1 (
    .in0(2'b00), .in1(2'b01), .in2(2'b10), .in3(2'b11), .out(WBSel), .sel(bitfinder_1_index));
  BitFinder #(.width(4)) bitfinder_1 (
    .in({is_lui, OUT10_PC_4, OUT01_ALU, is_I_load}), .index(bitfinder_1_index));  // open: found

  // Other names for the same wires on the sheet: OUT00_Mem = is_I_load; OUT11_NOPE = is_lui; funct3[2:0] = func3

  // Notes on the sheet:
  //   INPUT
  //   OUTPUT
endmodule
